# Fritzing sketch Tennis_Zero_Pi (saved by Fritzing 0.9.9b)
breadboards: 1

parts:
  MCU1 = Raspberry Pi Zero
  Part1 = Adafruit T-Cobbler Plus [part_number="Adafruit #1989 and #2028"]
  R1 = Rotary Potentiometer (Small) [maximum_resistance=100kΩ package=THT]
  OLED_I2C1 = OLED 128x64 I2C Monochrome Display
  Part2 = Adafruit PCF8591 [part_number="Adafruit #4648"]

nets:
  GND: MCU1.pin_3, MCU1.pin_4, Part1.GND, R1.leg2, OLED_I2C1.GND, Part2.GND
  +5V: MCU1.pin_5, MCU1.pin_6, MCU1.pin_9, MCU1.pin_12, MCU1.pin_14, MCU1.pin_16, MCU1.pin_18, MCU1.pin_20, MCU1.pin_25, MCU1.pin_26, MCU1.pin_27, MCU1.pin_28, MCU1.pin_29, MCU1.pin_30, MCU1.pin_31, MCU1.pin_32, MCU1.pin_33, MCU1.pin_34, MCU1.pin_39, MCU1.pin_40, Part1.+5V, R1.leg1, OLED_I2C1.VDD, Part2.VCC
  N1: MCU1.pin_11, MCU1.pin_13, MCU1.pin_15, MCU1.pin_17, MCU1.pin_19
  N2: Part1.SDA, Part2.SDA
  N3: Part1.SCL, Part2.SCL

custom parts:
  Adafruit T-Cobbler Plus: The Raspberry Pi has landed on the Maker World like a 40-GPIO pinned, quad-USB ported, credit card sized bomb of DIY joy. And while you can use most of our great Model B accessories by hooking up our downgrade cable, its probably a good time to upgrade your set up and accessorize using all of the 40 pins. That's why we now carry the Assembled Adafruit Pi T-Cobbler Plus - Breakout + Cable for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
  Adafruit PCF8591: Measuring voltage and adjusting it is what electronics is all about so you won’t get far without friends like the PCF8591 ADC+DAC combo. Analog to Digital Converters help by measuring an analog voltage and turning it into something a microcontroller like a Metro or Arduino can understand. If you’re using a single board computer like a Raspberry Pi, you might not have any other way to measure a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
